# Fritzing sketch coindrop (saved by Fritzing 0.8.5b)
breadboards: 1

parts:
  Part1 = Arduino Uno (Rev3)
  LED1 = LED - 5mm [color="White (8000K)" package="5 mm [THT]"]
  R1 = Photocell (LDR) [package=THT]
  R2 = Resistor [tolerance=±5% resistance=150 package=THT]
  R3 = Rotary Potentiometer (Small) [maximum_resistance=10kΩ package=THT]
  R4 = Resistor [tolerance=±5% resistance=220 package=THT]

nets:
  N1: Part1.A0, R1.pin_0, R2.Pin_1
  N2: Part1.A1, R3.wiper
  N3: Part1.5V, R2.Pin_0, R3.leg1, R4.Pin_1
  N4: Part1.GND, LED1.cathode, R1.pin_1, R3.leg2
  N5: LED1.anode, R4.Pin_0
